# Fritzing sketch Electrical Scheme BROWS (saved by Fritzing 0.9.3b)
breadboards: 2

parts:
  Componente1 = Arduino Uno (Rev3)
  RE2 = Rotary Encoder [package=THT]
  R26 = Resistor [tolerance=±5% resistance=1k package=THT]
  LED7 = smd LED [color="Red (633nm)" package="0805 [SMD]"]
  R27 = Resistor [tolerance=±5% resistance=1k package=THT]
  R28 = Resistor [tolerance=±5% resistance=1k package=THT]
  R29 = Resistor [tolerance=±5% resistance=1k package=THT]
  LED8 = smd LED [color="Red (633nm)" package="0805 [SMD]"]
  LED9 = smd LED [color="Red (633nm)" package="0805 [SMD]"]
  LED10 = smd LED [color="Red (633nm)" package="0805 [SMD]"]
  S1 = Pushbutton [package="[THT]"]
  S2 = Pushbutton [package="[THT]"]
  S3 = Pushbutton [package="[THT]"]
  S4 = Pushbutton [package="[THT]"]
  R30 = Resistor [tolerance=±5% resistance=220 package=THT]
  R31 = Resistor [tolerance=±5% resistance=220 package=THT]
  R32 = Resistor [tolerance=±5% resistance=220 package=THT]
  R33 = Resistor [tolerance=±5% resistance=220 package=THT]

nets:
  N1: Componente1.D8, S4.Pin_3, S4.Pin_4, R33.Pin_0
  N2: Componente1.D9_PWM, R29.Pin_0
  N3: Componente1.D10_PWM/SS, R28.Pin_0
  N4: Componente1.D11_PWM/MOSI, R27.Pin_0
  N5: Componente1.D12/MISO, R26.Pin_0
  N6: Componente1.D4, RE2.EncoderPinB
  N7: Componente1.D5_PWM, S1.Pin_3, S1.Pin_4, R30.Pin_0
  N8: Componente1.D6_PWM, S2.Pin_3, S2.Pin_4, R31.Pin_0
  N9: Componente1.D7, S3.Pin_3, S3.Pin_4, R32.Pin_0
  N10: Componente1.5V, RE2.EncoderPinC, S1.Pin_1, S1.Pin_2, S2.Pin_1, S2.Pin_2, S3.Pin_1, S3.Pin_2, S4.Pin_1, S4.Pin_2
  N11: Componente1.GND, RE2.EncoderPinA, LED7.cathode, LED8.cathode, LED9.cathode, LED10.cathode, R30.Pin_1, R31.Pin_1, R32.Pin_1, R33.Pin_1
  N12: R26.Pin_1, LED7.anode
  N13: R27.Pin_1, LED8.anode
  N14: R28.Pin_1, LED9.anode
  N15: R29.Pin_1, LED10.anode

notes:
  Ordem dos pinos do Rotary da esquerda pra direita:
  GND
  + (alimentação)
  SW(botão)
  DT (pino3)
  CLK(pino2)
